# Fritzing sketch pcb_version2 (saved by Fritzing 0.8.0b)
breadboards: 1

parts:
  PART1 = ML8511 UV Sensor Breakout [part_number=SEN-12705]
  Part1 = Arduino Pro Mini v13
  DIGITAL_POTENTIOMETER_/_MCP4131 = IC, DIP package, 8 pins [chip_label=IC]
  R1_-_4_7K = Resistor [tolerance=±5% resistance=470 package=THT]
  regulator = Voltage Regulator - 3.3V [package="TO220 [THT]"]

nets:
  N1: PART1.EN, PART1.3.3V, Part1.A1, regulator.output_voltage
  N2: PART1.OUT, Part1.A0
  GND: PART1.GND, Part1.GND, DIGITAL_POTENTIOMETER_/_MCP4131.pin4, DIGITAL_POTENTIOMETER_/_MCP4131.pin7, regulator.GND
  N3: Part1.VCC, DIGITAL_POTENTIOMETER_/_MCP4131.pin5, regulator.input_voltage
  N4: Part1.D13/SCK, DIGITAL_POTENTIOMETER_/_MCP4131.pin2
  N5: Part1.D12/MISO, R1_-_4_7K.Pin_0
  N6: Part1.D11_PWM/MOSI, DIGITAL_POTENTIOMETER_/_MCP4131.pin3, R1_-_4_7K.Pin_1
  N7: Part1.D10_PWM/SS, DIGITAL_POTENTIOMETER_/_MCP4131.pin1

notes:
  NOT LED... SILVER ELECTRODES
  fii.to

custom parts:
  ML8511 UV Sensor Breakout: Description: The ML8511 breakout is an easy to use ultraviolet light sensor. The MP8511 UV Sensor works by outputing an analog signal in relation to the amount of UV light it detects. This breakout can be very handy in creating devices that warn the user of sunburn or detect the UV index as it relates to weather conditions. This sensor breakout can detect 280-390nm light most effectively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
